// Logisim project Codificador.circ as structural Verilog
module Codificador (
  input  E0,
  input  E1,
  input  E2,
  input  E3,
  input  E4,
  input  E5,
  input  E6,
  input  E7,
  input  E8,
  input  E9,
  output SA,
  output SB,
  output SC,
  output SD
);

  wire not_1_out, not_2_out, not_3_out, not_4_out, not_5_out, not_6_out, not_7_out, not_8_out, not_9_out,
       not_10_out, not_11_out, not_12_out, not_13_out, not_14_out, not_15_out, not_16_out, not_17_out,
       not_18_out, not_19_out, not_20_out, not_21_out, not_22_out, not_23_out, not_24_out, not_25_out;

  not not_1 (not_1_out, E0);
  not not_2 (not_2_out, E1);
  not not_3 (not_3_out, E2);
  not not_4 (not_4_out, E3);
  not not_5 (not_5_out, E4);
  not not_6 (not_6_out, E5);
  not not_7 (not_7_out, E6);
  not not_8 (not_8_out, E7);
  not not_9 (not_9_out, E0);
  not not_10 (not_10_out, E1);
  not not_11 (not_11_out, E2);
  not not_12 (not_12_out, E3);
  not not_13 (not_13_out, E8);
  not not_14 (not_14_out, E9);
  not not_15 (not_15_out, E0);
  not not_16 (not_16_out, E1);
  not not_17 (not_17_out, E4);
  not not_18 (not_18_out, E5);
  not not_19 (not_19_out, E8);
  not not_20 (not_20_out, E9);
  not not_21 (not_21_out, E0);
  not not_22 (not_22_out, E2);
  not not_23 (not_23_out, E4);
  not not_24 (not_24_out, E6);
  not not_25 (not_25_out, E8);
  and and_1 (SA, not_1_out, not_2_out, not_3_out, not_4_out, not_5_out, not_6_out, not_7_out, not_8_out);
  and and_2 (SB, not_9_out, not_10_out, not_11_out, not_12_out, not_13_out, not_14_out);
  and and_3 (SC, not_15_out, not_16_out, not_17_out, not_18_out, not_19_out, not_20_out);
  and and_4 (SD, not_21_out, not_22_out, not_23_out, not_24_out, not_25_out);
endmodule
