// Logisim project Contador de 00 a 18 - incompleto.circ as structural Verilog: 1 circuit, main circuit main
module main (
);

  wire and_1_out, and_2_out, and_3_out, clock_1_out, decodificador_1_a_2, decodificador_1_b_2,
       decodificador_1_c_2, decodificador_1_d_2, decodificador_1_e, decodificador_1_f, decodificador_1_g,
       decodificador_2_a_2, decodificador_2_b_2, decodificador_2_c_2, decodificador_2_d_2, decodificador_2_e,
       decodificador_2_f, decodificador_2_g, main_1_q0, main_1_q1, main_1_q2, main_1_q3, main_2_q0,
       main_2_q1, main_2_q2, main_2_q3, or_1_out, or_2_out;

  and and_1 (and_1_out, main_1_q1, main_1_q1);
  or or_1 (or_1_out, and_1_out, and_2_out);
  FF_Contador__de_0_a_10_main main_1 (
    .Clock(and_3_out), .Reset(or_1_out), .Q3(main_1_q3), .Q2(main_1_q2), .Q1(main_1_q1), .Q0(main_1_q0));
  and and_2 (and_2_out, main_1_q0, main_2_q3, main_2_q0);
  or or_2 (or_2_out, and_2_out, and_3_out);
  Decodificador decodificador_1 (
    .A(main_1_q3), .B(main_1_q2), .C(main_1_q1), .D(main_1_q0), .a_2(decodificador_1_a_2),
    .b_2(decodificador_1_b_2), .c_2(decodificador_1_c_2), .d_2(decodificador_1_d_2), .e(decodificador_1_e),
    .f(decodificador_1_f), .g(decodificador_1_g));
  and and_3 (and_3_out, main_2_q3, main_2_q0);
  _7_Segment_Display u_7_segment_display_1 (
    .g(decodificador_1_g), .f(decodificador_1_f), .a(decodificador_1_a_2), .b(decodificador_1_b_2),
    .e(decodificador_1_e), .d(decodificador_1_d_2), .c(decodificador_1_c_2));  // open: dp
  Clock clock_1 (.out(clock_1_out));
  FF_Contador__de_0_a_10_main main_2 (
    .Clock(clock_1_out), .Reset(or_2_out), .Q3(main_2_q3), .Q2(main_2_q2), .Q1(main_2_q1), .Q0(main_2_q0));
  Decodificador decodificador_2 (
    .A(main_2_q3), .B(main_2_q2), .C(main_2_q1), .D(main_2_q0), .a_2(decodificador_2_a_2),
    .b_2(decodificador_2_b_2), .c_2(decodificador_2_c_2), .d_2(decodificador_2_d_2), .e(decodificador_2_e),
    .f(decodificador_2_f), .g(decodificador_2_g));
  _7_Segment_Display u_7_segment_display_2 (
    .g(decodificador_2_g), .f(decodificador_2_f), .a(decodificador_2_a_2), .b(decodificador_2_b_2),
    .e(decodificador_2_e), .d(decodificador_2_d_2), .c(decodificador_2_c_2));  // open: dp
endmodule
