// Logisim project Contador de 99 a 00.circ as structural Verilog: 1 circuit, main circuit main
module main (
  input  E,
  output Q3,
  output Q2,
  output Q1,
  output Q0
);

  wire and_1_out, and_2_out, J1_out, J2_out, J3_out, j_k_ff_1_qn, j_k_ff_2_qn, j_k_ff_3_qn, j_k_ff_4_qn,
       K2_out;

  J_K_Flip_Flop j_k_ff_1 (.J(J3_out), .clk(E), .K(j_k_ff_4_qn), .Q(Q3), .Qn(j_k_ff_1_qn));  // open: preset, en, reset
  J_K_Flip_Flop j_k_ff_2 (.J(J2_out), .clk(E), .K(K2_out), .Q(Q2), .Qn(j_k_ff_2_qn));  // open: preset, en, reset
  J_K_Flip_Flop j_k_ff_3 (.J(J1_out), .clk(E), .K(j_k_ff_4_qn), .Q(Q1), .Qn(j_k_ff_3_qn));  // open: preset, en, reset
  J_K_Flip_Flop j_k_ff_4 (.J(1'b1), .clk(E), .K(1'b1), .Q(Q0), .Qn(j_k_ff_4_qn));  // open: preset, en, reset
  and and_1 (and_1_out, Q2, j_k_ff_4_qn);
  or J1 (J1_out, and_1_out, and_2_out);
  and and_2 (and_2_out, Q3, j_k_ff_4_qn);
  and J2 (J2_out, Q3, j_k_ff_4_qn);
  and K2 (K2_out, j_k_ff_3_qn, j_k_ff_4_qn);
  and J3 (J3_out, j_k_ff_2_qn, j_k_ff_3_qn, j_k_ff_4_qn);
endmodule
