// Logisim project Contador, 0 a 3.circ as structural Verilog: 1 circuit, main circuit main
module main (
  input  Clock,
  output Q1,
  output Q0
);

  J_K_Flip_Flop j_k_ff_1 (.J(Q0), .clk(Clock), .K(Q0), .Q(Q1));  // open: Qn, preset, en, reset
  J_K_Flip_Flop j_k_ff_2 (.J(1'b1), .clk(Clock), .K(1'b1), .Q(Q0));  // open: Qn, preset, en, reset
endmodule
