// Logisim project MUX 2 por 1.circ as structural Verilog
module MUX_2_1 (
  input  E0,
  input  E1,
  input  A,
  output S
);

  wire and_1_out, and_2_out, not_1_out;

  not not_1 (not_1_out, A);
  and and_1 (and_1_out, E1, A);
  and and_2 (and_2_out, E0, not_1_out);
  or or_1 (S, and_1_out, and_2_out);
endmodule
