// Logisim project relógio de 0 a 3.circ as structural Verilog: 1 circuit, main circuit main
module main (
);

  wire clock_1_out, decodificador_1_a_2, decodificador_1_b_2, decodificador_1_c_2, decodificador_1_d_2,
       decodificador_1_e, decodificador_1_f, decodificador_1_g, main_1_q0, main_1_q1;

  Clock clock_1 (.out(clock_1_out));
  Contador__0_a_3_main main_1 (.Clock(clock_1_out), .Q1(main_1_q1), .Q0(main_1_q0));
  Decodificador decodificador_1 (
    .A(1'b0), .B(1'b0), .C(main_1_q1), .D(main_1_q0), .a_2(decodificador_1_a_2), .b_2(decodificador_1_b_2),
    .c_2(decodificador_1_c_2), .d_2(decodificador_1_d_2), .e(decodificador_1_e), .f(decodificador_1_f),
    .g(decodificador_1_g));
  _7_Segment_Display u_7_segment_display_1 (
    .g(decodificador_1_g), .f(decodificador_1_f), .a(decodificador_1_a_2), .b(decodificador_1_b_2),
    .e(decodificador_1_e), .d(decodificador_1_d_2), .c(decodificador_1_c_2));  // open: dp
endmodule
