// Logisim project C2 final.circ as structural Verilog: 1 circuit, main circuit main
module main (
  input  A,
  input  B,
  input  C,
  input  D
);

  wire decodificador_1_a_2, decodificador_1_b_2, decodificador_1_c_2, decodificador_1_d_2, decodificador_1_e,
       decodificador_1_f, decodificador_1_g, main_1_sa, main_1_sb, main_1_sc, main_1_sd;

  C2_positivo_e_negativo_main main_1 (
    .A(A), .B(B), .C(C), .D(D), .SA(main_1_sa), .SB(main_1_sb), .SC(main_1_sc), .SD(main_1_sd));
  Decodificador decodificador_1 (
    .A(main_1_sa), .B(main_1_sb), .C(main_1_sc), .D(main_1_sd), .a_2(decodificador_1_a_2),
    .b_2(decodificador_1_b_2), .c_2(decodificador_1_c_2), .d_2(decodificador_1_d_2), .e(decodificador_1_e),
    .f(decodificador_1_f), .g(decodificador_1_g));
  _7_Segment_Display u_7_segment_display_1 (
    .g(decodificador_1_g), .f(decodificador_1_f), .a(decodificador_1_a_2), .b(decodificador_1_b_2),
    .e(decodificador_1_e), .d(decodificador_1_d_2), .c(decodificador_1_c_2));  // open: dp
  _7_Segment_Display u_7_segment_display_2 (.g(A));  // open: f, a, b, e, d, c, dp
endmodule
