// Logisim project C2 positivo e negativo.circ as structural Verilog: 1 circuit, main circuit main
module main (
  input  A,
  input  B,
  input  C,
  input  D,
  output SA,
  output SB,
  output SC,
  output SD
);

  wire A_s0, A_s1, B_s0, B_s1, C_s0, C_s1, complemento_de_dois_1_sa, complemento_de_dois_1_sb,
       complemento_de_dois_1_sc, complemento_de_dois_1_sd, D_s0, D_s1;

  DEMUX_2_1 u_A (.E(A), .A(A), .S0(A_s0), .S1(A_s1));
  DEMUX_2_1 u_B (.E(B), .A(A), .S0(B_s0), .S1(B_s1));
  DEMUX_2_1 u_C (.E(C), .A(A), .S0(C_s0), .S1(C_s1));
  DEMUX_2_1 u_D (.E(D), .A(A), .S0(D_s0), .S1(D_s1));
  Complemento_de_dois complemento_de_dois_1 (
    .A(A_s1), .B(B_s1), .C(C_s1), .D(D_s1), .SA(complemento_de_dois_1_sa), .SB(complemento_de_dois_1_sb),
    .SC(complemento_de_dois_1_sc), .SD(complemento_de_dois_1_sd));
  or A_2 (SA, complemento_de_dois_1_sa, A_s0);
  or B_2 (SB, complemento_de_dois_1_sb, B_s0);
  or C_2 (SC, complemento_de_dois_1_sc, C_s0);
  or D_2 (SD, complemento_de_dois_1_sd, D_s0);
endmodule
