// Logisim project Complemento de dois.circ as structural Verilog
module Complemento_de_dois (
  input  A,
  input  B,
  input  C,
  input  D,
  output SA,
  output SB,
  output SC,
  output SD
);

  wire and_1_out, and_2_out, and_3_out, and_4_out, and_5_out, and_6_out, and_7_out, and_8_out, and_9_out,
       not_1_out, not_2_out, not_3_out, not_4_out, not_5_out, not_6_out, not_7_out, not_8_out, not_9_out,
       not_10_out, not_11_out, not_12_out;

  not not_1 (not_1_out, A);
  not not_2 (not_2_out, A);
  not not_3 (not_3_out, A);
  not not_4 (not_4_out, B);
  not not_5 (not_5_out, C);
  not not_6 (not_6_out, D);
  not not_7 (not_7_out, B);
  and and_1 (and_1_out, not_7_out, D);
  not not_8 (not_8_out, B);
  and and_2 (and_2_out, not_8_out, C);
  not not_9 (not_9_out, C);
  and and_3 (and_3_out, B, not_9_out, not_10_out);
  not not_10 (not_10_out, D);
  not not_11 (not_11_out, C);
  and and_4 (and_4_out, not_11_out, D);
  and and_5 (and_5_out, C, not_12_out);
  not not_12 (not_12_out, D);
  and and_6 (and_6_out, not_1_out, D);
  and and_7 (and_7_out, not_2_out, C);
  and and_8 (and_8_out, not_3_out, B);
  and and_9 (and_9_out, A, not_4_out, not_5_out, not_6_out);
  or or_1 (SB, and_1_out, and_2_out, and_3_out);
  or or_2 (SC, and_4_out, and_5_out);
  or or_3 (SA, and_6_out, and_7_out, and_8_out, and_9_out);

  assign SD = D;
endmodule
