// Logisim project DEMUX 1 por 2.circ as structural Verilog
module DEMUX_2_1 (
  input  E,
  input  A,
  output S0,
  output S1
);

  wire not_1_out;

  not not_1 (not_1_out, A);
  and and_1 (S1, E, A);
  and and_2 (S0, E, not_1_out);
endmodule
