// Logisim project FF_Contador, de 0 a 10.circ as structural Verilog: 1 circuit, main circuit main
module main (
  input  Clock,
  input  Reset,
  output Q3,
  output Q2,
  output Q1,
  output Q0
);

  wire j_k_ff_1_qn, j_k_ff_3_qn, or_1_out, or_2_out, Q0_Q1_2_out, Q0_Q1_out;

  and Q0_Q1 (Q0_Q1_out, Q0_Q1_2_out, Q2);
  J_K_Flip_Flop j_k_ff_1 (
    .J(Q0_Q1_out), .clk(Clock), .K(Q1), .Q(Q3), .Qn(j_k_ff_1_qn), .reset(Reset));  // open: preset, en
  and Q0_Q1_2 (Q0_Q1_2_out, Q1, Q0);
  or or_1 (or_1_out, Q3, Q0);
  J_K_Flip_Flop j_k_ff_2 (
    .J(Q0_Q1_2_out), .clk(Clock), .K(Q0_Q1_2_out), .Q(Q2), .reset(Reset));  // open: Qn, preset, en
  J_K_Flip_Flop j_k_ff_3 (
    .J(Q0), .clk(Clock), .K(or_1_out), .Q(Q1), .Qn(j_k_ff_3_qn), .reset(Reset));  // open: preset, en
  or or_2 (or_2_out, j_k_ff_3_qn, j_k_ff_1_qn);
  J_K_Flip_Flop j_k_ff_4 (.J(or_2_out), .clk(Clock), .K(1'b1), .Q(Q0), .reset(Reset));  // open: Qn, preset, en
endmodule
