// Logisim project MUX 2 por 1.circ as structural Verilog
module MUX_2_1 (
  input  A,
  input  E0,
  input  E1,
  output S
);

  wire and_1_out, and_2_out, not_1_out;

  not not_1 (not_1_out, A);
  and and_1 (and_1_out, not_1_out, E0);
  and and_2 (and_2_out, A, E1);
  or or_1 (S, and_1_out, and_2_out);
endmodule
