// Logisim project MUX 4 por 1.circ as structural Verilog: 1 circuit, main circuit main
module main (
  input  E0,
  input  E1,
  input  E2,
  input  E3,
  input  C0,
  input  C1,
  output S
);

  wire mux_2_1_1_p4, mux_2_1_2_p4;

  // MUX_2_1 mux_2_1_1: pin names not known; wires that end beside it: E0, E1, C0, mux_2_1_1_p4
  // MUX_2_1 mux_2_1_2: pin names not known; wires that end beside it: E2, E3, C0, mux_2_1_2_p4
  // MUX_2_1 mux_2_1_3: pin names not known; wires that end beside it: mux_2_1_1_p4, mux_2_1_2_p4, C1, S
endmodule
