// Logisim project Somador 4 bits.circ as structural Verilog: 1 circuit, main circuit main
module main (
  input  A3,
  input  A2,
  input  A1,
  input  A0,
  input  B3,
  input  B2,
  input  B1,
  input  B0,
  output out_9,
  output out_10,
  output out_11,
  output out_12
);

  wire somador_completo_2_cout, somador_completo_3_cout, somador_completo_4_cout;

  Somador_completo somador_completo_1 (.A(A3), .B(B3), .Cin(somador_completo_2_cout), .S(out_9));  // open: Cout
  Somador_completo somador_completo_2 (
    .A(A2), .B(B2), .Cin(somador_completo_3_cout), .S(out_10), .Cout(somador_completo_2_cout));
  Somador_completo somador_completo_3 (
    .A(A1), .B(B1), .Cin(somador_completo_4_cout), .S(out_11), .Cout(somador_completo_3_cout));
  Somador_completo somador_completo_4 (.A(A0), .B(B0), .Cin(1'b0), .S(out_12), .Cout(somador_completo_4_cout));
endmodule
