// Logisim project Subtrator de 4 bits.circ as structural Verilog: 1 circuit, main circuit main
module main (
  input  A3,
  input  A2,
  input  A1,
  input  A0,
  input  B3,
  input  B2,
  input  B1,
  input  B0,
  output S3,
  output S2,
  output S1,
  output S0
);

  wire subtrator_completo_2_bout, subtrator_completo_3_bout, subtrator_completo_4_bout;

  Subtrator_Completo subtrator_completo_1 (.A(A3), .B(B3), .Cin(subtrator_completo_2_bout), .A_2(S3));  // open: Bout
  Subtrator_Completo subtrator_completo_2 (
    .A(A2), .B(B2), .Cin(subtrator_completo_3_bout), .A_2(S2), .Bout(subtrator_completo_2_bout));
  Subtrator_Completo subtrator_completo_3 (
    .A(A1), .B(B1), .Cin(subtrator_completo_4_bout), .A_2(S1), .Bout(subtrator_completo_3_bout));
  Subtrator_Completo subtrator_completo_4 (.A(A0), .B(B0), .Cin(1'b0), .A_2(S0), .Bout(subtrator_completo_4_bout));
endmodule
