// Logisim project Teclado numérico.circ as structural Verilog: 1 circuit, main circuit main
module main (
);

  wire _0_out, _1_out, _2_out, _3_out, _4_out, _5_out, _6_out, _7_out, _8_out, _9_out, codificador_1_sa,
       codificador_1_sb, codificador_1_sc, codificador_1_sd, decodificador_1_a_2, decodificador_1_b_2,
       decodificador_1_c_2, decodificador_1_d_2, decodificador_1_e, decodificador_1_f, decodificador_1_g;

  Button _8 (.out(_8_out));
  Button _7 (.out(_7_out));
  Button _4 (.out(_4_out));
  Button _5 (.out(_5_out));
  Button _2 (.out(_2_out));
  Button _1 (.out(_1_out));
  Button _0 (.out(_0_out));
  Button _9 (.out(_9_out));
  Button _6 (.out(_6_out));
  Button _3 (.out(_3_out));
  Codificador codificador_1 (
    .E0(_0_out), .E1(_1_out), .E2(_2_out), .E3(_3_out), .E4(_4_out), .E5(_5_out), .E6(_6_out), .E7(_7_out),
    .E8(_8_out), .E9(_9_out), .SA(codificador_1_sa), .SB(codificador_1_sb), .SC(codificador_1_sc),
    .SD(codificador_1_sd));
  Decodificador decodificador_1 (
    .A(codificador_1_sa), .B(codificador_1_sb), .C(codificador_1_sc), .D(codificador_1_sd),
    .a_2(decodificador_1_a_2), .b_2(decodificador_1_b_2), .c_2(decodificador_1_c_2),
    .d_2(decodificador_1_d_2), .e(decodificador_1_e), .f(decodificador_1_f), .g(decodificador_1_g));
  _7_Segment_Display u_7_segment_display_1 (
    .g(decodificador_1_g), .f(decodificador_1_f), .a(decodificador_1_a_2), .b(decodificador_1_b_2),
    .e(decodificador_1_e), .d(decodificador_1_d_2), .c(decodificador_1_c_2));  // open: dp
endmodule
